// Logisim project atividade1.circ as structural Verilog: 1 circuit, main circuit main
module main (
  input  a,
  input  b,
  output z1__NOT_a,
  output z2__NOT_b,
  output z3__AND,
  output z4__OR,
  output z5__NAND,
  output z6__NOR,
  output z7__XOR,
  output z8__XNOR
);

  wire undriven;

  not not_1 (z1__NOT_a, undriven);
  not not_2 (z2__NOT_b, b);
  and and_1 (z3__AND, undriven, b);
  or or_1 (z4__OR, a, b);
  nand nand_1 (z5__NAND, undriven, b);
  nor nor_1 (z6__NOR, undriven, b);
  xor xor_1 (z7__XOR, undriven, b);
  xnor xnor_1 (z8__XNOR, undriven, b);
endmodule
